# Fritzing sketch sketch (saved by Fritzing 0.9.3b)

parts:
  R1 = Resistor [tolerance=±5% resistance=4.7k package=THT]
  U1 = NodeMCU V1.0
  LCM1602_IIC2 = LCM1602 IIC [part_number="LCM1602 IIC" chip_label="LCM1602 IIC" package="DIP (Dual Inline) [THT]"]
  LCD1_20x5 = LCD screen
  DS2 = DS18B20 1-Wire Temperature Sensor Probe Cable
  DS3 = DS18B20 1-Wire Temperature Sensor Probe Cable
  DS1 = DS18B20 1-Wire Temperature Sensor Probe Cable
  S1 = Pushbutton [package="[THT]"]

nets:
  N1: R1.Pin_0, U1.D4, DS2.DQ, DS3.DQ, DS1.DQ
  VDD: R1.Pin_1, U1.3V3, DS2.VDD, DS3.VDD, DS1.VDD
  N2: U1.D1, LCM1602_IIC2.SCL
  N3: U1.D2, LCM1602_IIC2.SDA
  GND: U1.D3, U1.GND, LCM1602_IIC2.GND, DS1.GND, S1.Pin_3, S1.Pin_4
  VIN: U1.Vin, LCM1602_IIC2.VCC
  VSS: LCM1602_IIC2.VSS, LCD1_20x5.VSS
  VDD_2: LCM1602_IIC2.VDD, LCD1_20x5.VDD
  N4: LCM1602_IIC2.V0, LCD1_20x5.V0
  N5: LCM1602_IIC2.RS, LCD1_20x5.RS
  N6: LCM1602_IIC2.RW, LCD1_20x5.R/W
  N7: LCM1602_IIC2.E, LCD1_20x5.E
  N8: LCM1602_IIC2.D0, LCD1_20x5.DB0
  N9: LCM1602_IIC2.D1, LCD1_20x5.DB1
  N10: LCM1602_IIC2.D2, LCD1_20x5.DB2
  N11: LCM1602_IIC2.D3, LCD1_20x5.DB3
  N12: LCM1602_IIC2.D4, LCD1_20x5.DB4
  N13: LCM1602_IIC2.D5, LCD1_20x5.DB5
  N14: LCM1602_IIC2.D6, LCD1_20x5.DB6
  N15: LCM1602_IIC2.D7, LCD1_20x5.DB7
  N16: LCM1602_IIC2.A, LCD1_20x5.LED-
  N17: LCM1602_IIC2.K, LCD1_20x5.LED+

custom parts:
  NodeMCU V1.0: ESP8266 based NodeMCU
  LCM1602 IIC: I2C-Module to use a 1602 or 2004 LCD on with the wire.h libory Serial LCD Modul
  LCD screen: A standard character display, usually with 2x16 characters. Comes in many colors.
